// Logisim project MIPS_Simulation_B2.circ as structural Verilog: 6 circuits, main circuit main
module main (
  input  CLR
);

  wire alu_1_zero_flag, CLK_out, control_1_alusrc, control_1_beq, control_1_bneq, control_1_jump,
       control_1_memread, control_1_memtoreg, control_1_memwrite, control_1_regdst, control_1_regwrite,
       multiplexer_4_out;
  wire [2:0] control_1_aluop;
  wire [3:0] alu_1_output, data_memory_1_data_read, instruction_1__0_3, instruction_1__4_7,
       instruction_1__8_11, instruction_1_opcode, multiplexer_1_out, multiplexer_2_out, multiplexer_6_out,
       registers_1_read_data_1, registers_1_read_data_2;
  wire [7:0] adder_1_out, adder_2_out, bit_extender_1_out, instruction_1_jumpaddr, instruction_1_pc_read,
       multiplexer_3_out, multiplexer_5_out;
  wire [19:0] registers_1_t4__t3__t2__t1__t0;

  // Probe on multiplexer_5_out
  Clock CLK (.out(CLK_out));
  Adder adder_1 (.a(instruction_1_pc_read), .b(8'h1), .out(adder_1_out));  // open: cin, cout
  // Probe on instruction_1_pc_read
  // Probe on instruction_1_jumpaddr
  // Probe on instruction_1_opcode
  // Probe on instruction_1__8_11
  // Probe on instruction_1__4_7
  // Probe on instruction_1__0_3
  Instruction instruction_1 (
    .PC_Write(multiplexer_5_out), .Reset(CLR), .PC_Read(instruction_1_pc_read),
    .Opcode(instruction_1_opcode), ._8_11(instruction_1__8_11), ._4_7(instruction_1__4_7),
    ._0_3(instruction_1__0_3), .jumpAddr(instruction_1_jumpaddr), .Clock(CLK_out));
  assign bit_extender_1_out = {{4{1'b0}}, instruction_1__0_3};  // Bit_Extender bit_extender_1
  // Probe on multiplexer_1_out
  Multiplexer #(.width(4), .enable("false")) multiplexer_1 (
    .in0(instruction_1__4_7), .in1(instruction_1__0_3), .out(multiplexer_1_out), .sel(control_1_regdst));
  Adder adder_2 (.a(bit_extender_1_out), .b(adder_1_out), .out(adder_2_out));  // open: cin, cout
  Control control_1 (
    .OP_Code(instruction_1_opcode), .ALUOp(control_1_aluop), .RegDst(control_1_regdst),
    .ALUSrc(control_1_alusrc), .MemToReg(control_1_memtoreg), .RegWrite(control_1_regwrite),
    .MemRead(control_1_memread), .MemWrite(control_1_memwrite), .beq(control_1_beq), .bneq(control_1_bneq),
    .Jump(control_1_jump));
  Registers registers_1 (
    .WriteReg_1(multiplexer_1_out), .WriteData(multiplexer_6_out), .ReadReg1(instruction_1__8_11),
    .ReadReg2(instruction_1__4_7), .RegWrite(control_1_regwrite), .CLK(CLK_out),
    .Read_Data_1(registers_1_read_data_1), .Read_Data_2(registers_1_read_data_2),
    .t4__t3__t2__t1__t0(registers_1_t4__t3__t2__t1__t0), .CLR(CLR));
  // Probe on registers_1_read_data_1
  // Probe on registers_1_read_data_2
  Multiplexer #(.width(4), .enable("false")) multiplexer_2 (
    .in0(registers_1_read_data_2), .in1(instruction_1__0_3), .out(multiplexer_2_out), .sel(control_1_alusrc));
  Multiplexer #(.width(8), .enable("false")) multiplexer_3 (
    .in0(adder_1_out), .in1(adder_2_out), .out(multiplexer_3_out), .sel(multiplexer_4_out));
  Multiplexer #(.enable("false")) multiplexer_4 (
    .in0(control_1_bneq), .in1(control_1_beq), .out(multiplexer_4_out), .sel(alu_1_zero_flag));
  // Probe on multiplexer_2_out
  // Probe on control_1_aluop
  // Probe on alu_1_zero_flag
  ALU alu_1 (
    .ALUOp(control_1_aluop), .A(registers_1_read_data_1), .B(multiplexer_2_out), .Output(alu_1_output),
    .Zero_flag(alu_1_zero_flag));
  Multiplexer #(.width(8), .enable("false")) multiplexer_5 (
    .in0(multiplexer_3_out), .in1(instruction_1_jumpaddr), .out(multiplexer_5_out), .sel(control_1_jump));
  // Probe on alu_1_output
  // Probe on registers_1_t4__t3__t2__t1__t0[19:16]
  // Probe on registers_1_t4__t3__t2__t1__t0[15:12]
  // Probe on registers_1_t4__t3__t2__t1__t0[11:8]
  // Probe on registers_1_t4__t3__t2__t1__t0[7:4]
  // Probe on registers_1_t4__t3__t2__t1__t0[3:0]
  // Probe on registers_1_read_data_2
  Data_Memory data_memory_1 (
    .Address(alu_1_output), .Write_Data(registers_1_read_data_2), .CLK(CLK_out),
    .Data_Read(data_memory_1_data_read), .MemRead(control_1_memread), .MemWrite(control_1_memwrite), .CLR(CLR));
  // Probe on data_memory_1_data_read
  Multiplexer #(.width(4), .enable("false")) multiplexer_6 (
    .in0(alu_1_output), .in1(data_memory_1_data_read), .out(multiplexer_6_out), .sel(control_1_memtoreg));
  // Probe on multiplexer_6_out
endmodule

module Registers (
  input  RegWrite,
  input  CLK,
  input  [3:0] WriteReg_1,
  input  [3:0] WriteData,
  input  CLR,
  input  [3:0] ReadReg1,
  input  [3:0] ReadReg2,
  output [19:0] t4__t3__t2__t1__t0,
  output [3:0] Read_Data_1,
  output [3:0] Read_Data_2
);

  wire and_1_out, demultiplexer_1_out1, demultiplexer_1_out2, demultiplexer_1_out3, demultiplexer_1_out4,
       demultiplexer_1_out6, demultiplexer_1_out7, not_1_out, not_2_out, not_3_out, not_4_out, not_5_out,
       not_6_out;
  wire [3:0] sp_q;

  not not_1 (not_1_out, demultiplexer_1_out1);
  Register #(.width(4)) t1 (.D(WriteData), .Q(t4__t3__t2__t1__t0[7:4]), .clk(not_1_out), .clr(CLR));  // open: en
  not not_2 (not_2_out, demultiplexer_1_out2);
  Register #(.width(4)) t2 (.D(WriteData), .Q(t4__t3__t2__t1__t0[11:8]), .clk(not_2_out), .clr(CLR));  // open: en
  Multiplexer #(.select(3), .width(4), .enable("false")) multiplexer_1 (
    .in0(4'b0000), .in1(t4__t3__t2__t1__t0[7:4]), .in2(t4__t3__t2__t1__t0[11:8]),
    .in3(t4__t3__t2__t1__t0[15:12]), .in4(t4__t3__t2__t1__t0[19:16]), .in5(4'b0000), .in6(sp_q),
    .in7(t4__t3__t2__t1__t0[3:0]), .out(Read_Data_1), .sel(ReadReg1[2:0]));
  Demultiplexer #(.select(3), .enable("false")) demultiplexer_1 (
    .out1(demultiplexer_1_out1), .out2(demultiplexer_1_out2), .out3(demultiplexer_1_out3),
    .out4(demultiplexer_1_out4), .out6(demultiplexer_1_out6), .out7(demultiplexer_1_out7), .in(and_1_out),
    .sel(WriteReg_1[2:0]));  // open: out0, out5
  not not_3 (not_3_out, demultiplexer_1_out3);
  Register #(.width(4)) t3 (.D(WriteData), .Q(t4__t3__t2__t1__t0[15:12]), .clk(not_3_out), .clr(CLR));  // open: en
  and and_1 (and_1_out, RegWrite, CLK);
  not not_4 (not_4_out, demultiplexer_1_out4);
  Register #(.width(4)) t4 (.D(WriteData), .Q(t4__t3__t2__t1__t0[19:16]), .clk(not_4_out), .clr(CLR));  // open: en
  Multiplexer #(.select(3), .width(4), .enable("false")) multiplexer_2 (
    .in0(4'b0000), .in1(t4__t3__t2__t1__t0[7:4]), .in2(t4__t3__t2__t1__t0[11:8]),
    .in3(t4__t3__t2__t1__t0[15:12]), .in4(t4__t3__t2__t1__t0[19:16]), .in5(4'b0000), .in6(sp_q),
    .in7(t4__t3__t2__t1__t0[3:0]), .out(Read_Data_2), .sel(ReadReg2[2:0]));
  not not_5 (not_5_out, demultiplexer_1_out7);
  Register #(.width(4)) t0 (.D(WriteData), .Q(t4__t3__t2__t1__t0[3:0]), .clk(not_5_out), .clr(CLR));  // open: en
  not not_6 (not_6_out, demultiplexer_1_out6);
  Register #(.width(4)) sp (.D(WriteData), .Q(sp_q), .clk(not_6_out), .clr(CLR));  // open: en

  // Notes on the sheet:
  //   $zero
endmodule

module Instruction (
  input  [7:0] PC_Write,
  input  Clock,
  input  Reset,
  output [7:0] PC_Read,
  output [3:0] Opcode,
  output [3:0] _8_11,
  output [3:0] _4_7,
  output [3:0] _0_3,
  output [7:0] jumpAddr
);

  Register #(.trigger("falling")) PC (.D(PC_Write), .Q(PC_Read), .clk(Clock), .clr(Reset));  // open: en
  ROM #(.dataWidth(16)) rom_1 (.addr(PC_Read), .data({Opcode, _8_11, _4_7, _0_3}), .sel(1'b1));

  assign jumpAddr = {_8_11, _4_7};

  // Notes on the sheet:
  //   contents of rom_1 (hex, n*v repeats v):
  //   d06f d06f 8075 4045 5742 d070 9080 d011 f000
endmodule

module Data_Memory (
  input  [3:0] Address,
  input  [3:0] Write_Data,
  input  MemWrite,
  input  MemRead,
  input  CLK,
  input  CLR,
  output [3:0] Data_Read
);

  wire not_1_out;

  not not_1 (not_1_out, CLK);
  RAM #(.addrWidth(4), .dataWidth(4), .bus("separate")) ram_1 (
    .addr(Address), .din(Write_Data), .data(Data_Read), .str(MemWrite), .clk(not_1_out), .ld(MemRead),
    .clr(CLR));  // open: sel
endmodule

module ALU (
  input  [2:0] ALUOp,
  input  [3:0] A,
  input  [3:0] B,
  output [3:0] Output,
  output Zero_flag
);

  wire [3:0] adder_1_out, and_1_out, nor_1_out, or_1_out, shifter_1_out, shifter_2_out, subtractor_1_out;

  Adder #(.width(4)) adder_1 (.a(A), .b(B), .out(adder_1_out), .cin(1'b0));  // open: cout
  Subtractor #(.width(4)) subtractor_1 (.a(A), .b(B), .out(subtractor_1_out), .bin(1'b0));  // open: bout
  assign and_1_out = A & B;  // AND_Gate and_1, 4 bits wide
  assign or_1_out = A | B;  // OR_Gate or_1, 4 bits wide
  assign nor_1_out = ~(A | B);  // NOR_Gate nor_1, 4 bits wide
  Shifter #(.width(4)) shifter_1 (.in(A), .\dist (B[1:0]), .out(shifter_1_out));
  Shifter #(.width(4), .shift("lr")) shifter_2 (.in(A), .\dist (B[1:0]), .out(shifter_2_out));
  Multiplexer #(.select(3), .width(4), .enable("false")) multiplexer_1 (
    .in0(adder_1_out), .in1(subtractor_1_out), .in2(and_1_out), .in3(or_1_out), .in4(nor_1_out),
    .in5(shifter_1_out), .in6(shifter_2_out), .in7(4'b0000), .out(Output), .sel(ALUOp));
  nor nor_2 (Zero_flag, Output[0], Output[1], Output[2], Output[3]);
endmodule

module Control (
  input  [3:0] OP_Code,
  output [2:0] ALUOp,
  output Jump,
  output bneq,
  output beq,
  output MemWrite,
  output MemRead,
  output RegWrite,
  output MemToReg,
  output ALUSrc,
  output RegDst
);

  ROM #(.addrWidth(4), .dataWidth(12)) rom_1 (
    .addr(OP_Code), .data({RegDst, ALUSrc, MemToReg, RegWrite, MemRead, MemWrite, beq, bneq, Jump, ALUOp}));  // open: sel

  // Notes on the sheet:
  //   contents of rom_1 (hex, n*v repeats v):
  //   904 503 901 505 780 21 502 501 640 8 11 902 903 500 506 900
endmodule
